# Fritzing sketch sketch model (saved by Fritzing 0.8.7b)
breadboards: 1

parts:
  Part1 = Arduino Nano (Rev3.0) (ICSP)
  R1 = Resistor [tolerance=±5% resistance=220 package=THT]
  R2 = Resistor [tolerance=±5% resistance=220 package=THT]
  J1 = Piezo Speaker
  R3 = Resistor [tolerance=±5% resistance=220 package=THT]
  LED1 = LED - 5mm [color="Red (633nm)" package="5 mm [THT]"]
  LED2 = LED - 5mm [color="Green (570nm)" package="5 mm [THT]"]
  S1 = Round Pushbutton
  R4 = Resistor [tolerance=±5% resistance=220 package=THT]

nets:
  N1: Part1.GND, R3.Pin_0, R4.Pin_0
  N2: Part1.D2, S1.leg1
  N3: Part1.D8, J1.pin2
  N4: Part1.D12/MISO, R1.Pin_0
  N5: Part1.D13/SCK, R2.Pin_0
  N6: R1.Pin_1, LED1.anode
  N7: R2.Pin_1, LED2.anode
  N8: J1.pin1, R3.Pin_1
  N9: S1.leg0, R4.Pin_1

notes:
  tugas tombol penyebrang jalan
  led hijau=D12
  ledmerah=D13
  buzzer=D8
  button=D12
